// Logisim project calculator.circ as structural Verilog
module UC (
  input  Input_1,
  input  Input_2,
  input  Input_3,
  input  Input_4,
  input  Input_5,
  input  Input_6,
  input  [15:0] Input_bus_1,
  input  Input_7,
  input  Input_8,
  input  Input_9,
  input  Input_10,
  input  Input_11,
  output [6:0] Output_bus_1,
  output [3:0] Output_bus_2,
  output Output_1,
  output [15:0] Output_bus_3,
  output Output_2,
  output [15:0] Output_bus_4,
  output [2:0] Output_bus_5,
  output Output_3
);

  wire debouncer_1_btn_clr, debouncer_2_btn_clr, debouncer_3_btn_clr, debouncer_4_btn_clr;
  wire [3:0] bin_bcd_1_hundreds, bin_bcd_1_ones, bin_bcd_1_tens, bin_bcd_1_thousands;
  wire [15:0] dmux_1_output1, dmux_1_output2, IN_operator_1_output_bus_1, mux_1_output,
       register_16bit_2_output;

  register_16bit register_16bit_2 (.\input (Input_bus_1), .clk(Input_2), .\output (register_16bit_2_output));
  IN_operator IN_operator_1 (
    .Input_1(Input_1), .Input_2(Input_2), .Input_3(Input_3), .Input_4(Input_4), .Input_5(Input_5),
    .Input_6(Input_6), .Output_bus_1(IN_operator_1_output_bus_1));
  debouncer debouncer_2 (.clk(Input_2), .btn(Input_8), .btn_clr(debouncer_2_btn_clr));
  mux mux_1 (
    .input1(register_16bit_2_output), .input2(IN_operator_1_output_bus_1), .sel(debouncer_2_btn_clr),
    .mode(Output_2), .\output (mux_1_output));
  debouncer debouncer_1 (.clk(Input_2), .btn(Input_7), .btn_clr(debouncer_1_btn_clr));
  debouncer debouncer_3 (.clk(Input_2), .btn(Input_9), .btn_clr(debouncer_3_btn_clr));
  debouncer debouncer_4 (.clk(Input_2), .btn(Input_10), .btn_clr(debouncer_4_btn_clr));
  debouncer debouncer_5 (.clk(Input_2), .btn(Input_11), .btn_clr(Output_3));
  bin_bcd bin_bcd_1 (
    .\input (mux_1_output), .ones(bin_bcd_1_ones), .tens(bin_bcd_1_tens), .hundreds(bin_bcd_1_hundreds),
    .thousands(bin_bcd_1_thousands), .semn(Output_1));
  dmux dmux_1 (
    .\input (mux_1_output), .adunare(debouncer_1_btn_clr), .inmultire(debouncer_3_btn_clr),
    .impartire(debouncer_4_btn_clr), .egal(Output_3), .output1(dmux_1_output1), .output2(dmux_1_output2),
    .operatie_aleasa(Output_bus_5));
  SSD ssd_1 (
    .digit0(bin_bcd_1_ones), .digit1(bin_bcd_1_tens), .digit2(bin_bcd_1_hundreds),
    .digit3(bin_bcd_1_thousands), .clk(Input_2), .catod(Output_bus_1), .anod(Output_bus_2));
  register_16bit register_16bit_1 (.\input (dmux_1_output1), .clk(Input_2), .\output (Output_bus_3));
  register_16bit register_16bit_3 (.\input (dmux_1_output2), .clk(Input_2), .\output (Output_bus_4));
endmodule

module UE (
  input  [15:0] Input_bus_1,
  input  [15:0] Input_bus_2,
  input  Input_1,
  input  [2:0] Input_bus_3,
  output [15:0] Output_bus_1
);

  wire [15:0] booth_multiplier_1_result, impartire_1_r, sumator_scazator_1_res;

  sumator_scazator sumator_scazator_1 (.a(Input_bus_1), .b(Input_bus_2), .res(sumator_scazator_1_res));
  booth_multiplier booth_multiplier_1 (.m(Input_bus_1), .r(Input_bus_2), .result(booth_multiplier_1_result));
  impartire impartire_1 (.X(Input_bus_1), .Y(Input_bus_2), .R(impartire_1_r));
  mux_ue mux_ue_1 (
    .input1(sumator_scazator_1_res), .input2(booth_multiplier_1_result), .input3(impartire_1_r),
    .salvare(Input_1), .sel(Input_bus_3), .\output (Output_bus_1));
endmodule

module IN_operator (
  input  Input_1,
  input  Input_2,
  input  Input_3,
  input  Input_4,
  input  Input_5,
  input  Input_6,
  output [15:0] Output_bus_1
);

  wire divizor_frecventa_1_clk_out;
  wire [3:0] counter_zecimal_1_cifra, counter_zecimal_2_cifra, counter_zecimal_3_cifra,
       counter_zecimal_4_cifra;

  divizor_frecventa divizor_frecventa_1 (.clk_in(Input_2), .clk_out(divizor_frecventa_1_clk_out));
  counter_zecimal counter_zecimal_1 (
    .clk_1s(divizor_frecventa_1_clk_out), .en(Input_1), .cifra(counter_zecimal_1_cifra));
  counter_zecimal counter_zecimal_3 (
    .clk_1s(divizor_frecventa_1_clk_out), .en(Input_5), .cifra(counter_zecimal_3_cifra));
  counter_zecimal counter_zecimal_4 (
    .clk_1s(divizor_frecventa_1_clk_out), .en(Input_6), .cifra(counter_zecimal_4_cifra));
  counter_zecimal counter_zecimal_2 (
    .clk_1s(divizor_frecventa_1_clk_out), .en(Input_3), .cifra(counter_zecimal_2_cifra));
  bcd_bin bcd_bin_1 (
    .bcd_in_0(counter_zecimal_1_cifra), .bcd_in_10(counter_zecimal_2_cifra),
    .bcd_in_100(counter_zecimal_3_cifra), .bcd_in_1000(counter_zecimal_4_cifra), .semn(Input_4),
    .bin_out(Output_bus_1));
endmodule

module CALC (
  input  Input_1,
  input  Input_2,
  input  Input_3,
  input  Input_4,
  input  Input_5,
  input  Input_6,
  input  Input_7,
  input  Input_8,
  input  Input_9,
  input  Input_10,
  input  Input_11,
  output [6:0] Output_bus_1,
  output [3:0] Output_bus_2,
  output Output_1,
  output Output_2,
  output [2:0] Output_bus_3
);

  wire UC_1_output_3;
  wire [15:0] UC_1_output_bus_3, UC_1_output_bus_4, UE_1_output_bus_1;

  UC UC_1 (
    .Input_1(Input_1), .Input_2(Input_2), .Input_3(Input_3), .Input_4(Input_4), .Input_5(Input_5),
    .Input_6(Input_6), .Input_bus_1(UE_1_output_bus_1), .Input_7(Input_7), .Input_8(Input_8),
    .Input_9(Input_9), .Input_10(Input_10), .Input_11(Input_11), .Output_bus_1(Output_bus_1),
    .Output_bus_2(Output_bus_2), .Output_1(Output_1), .Output_bus_3(UC_1_output_bus_3), .Output_2(Output_2),
    .Output_bus_4(UC_1_output_bus_4), .Output_bus_5(Output_bus_3), .Output_3(UC_1_output_3));
  UE UE_1 (
    .Input_bus_1(UC_1_output_bus_3), .Input_bus_2(UC_1_output_bus_4), .Input_1(UC_1_output_3),
    .Input_bus_3(Output_bus_3), .Output_bus_1(UE_1_output_bus_1));
endmodule

// VHDL entity counter_zecimal, as the project stores it:
LIBRARY ieee;
USE ieee.std_logic_1164.all;
use ieee.std_logic_unsigned.all;

ENTITY counter_zecimal IS
  PORT (
  	clk_1s: in std_logic;
  	en: in std_logic;
  	cifra: out std_logic_vector(3 downto 0)
    );
END counter_zecimal;


ARCHITECTURE TypeArchitecture OF counter_zecimal IS

BEGIN

counter: process(clk_1s, en)
variable aux: std_logic_vector(3 downto 0):="0000";

begin
	if clk_1s = '1' and clk_1s'event then
		if en = '0' then
			if aux >= "1001" then aux:="0000";
			else
			aux:= aux+'1';
			end if;
			cifra<=aux;
		else
			cifra<=aux;
		end if;
	
	end if;
end process counter;

END TypeArchitecture;

// VHDL entity SSD, as the project stores it:
library IEEE;
use IEEE.STD_LOGIC_1164.ALL;
use IEEE.STD_LOGIC_ARITH.ALL;
use IEEE.STD_LOGIC_UNSIGNED.ALL;

entity SSD is	--7 segments display
    Port ( digit0 : in STD_LOGIC_VECTOR (3 downto 0);
           digit1 : in STD_LOGIC_VECTOR (3 downto 0);
           digit2 : in STD_LOGIC_VECTOR (3 downto 0);
           digit3 : in STD_LOGIC_VECTOR (3 downto 0);
           clk : in STD_LOGIC;
           catod : out STD_LOGIC_VECTOR (6 downto 0);
           anod : out STD_LOGIC_VECTOR (3 downto 0));
end SSD;

architecture arch of SSD is

signal d: std_logic_vector(3 downto 0);
signal count:STD_LOGIC_VECTOR(15 downto 0);
constant full_counter: std_logic_vector(15 downto 0):=(others=>'1');

begin

process(d)
begin
    case d is
        when "0001" => catod <= not("1111001") ;   --1
        when "0010" => catod <= not("0100100") ;   --2
        when "0011" => catod <= not("0110000") ;   --3
        when "0100" => catod <= not("0011001") ;   --4
        when "0101" => catod <= not("0010010") ;   --5
        when "0110" => catod <= not("0000010") ;   --6
        when "0111" => catod <= not("1111000") ;   --7
        when "1000" => catod <= not("0000000") ;   --8
        when "1001" => catod <= not("0010000") ;   --9
        when others => catod <= not("1000000") ;   --0
    end case;
end process;

process(clk)
    begin
        if(rising_edge(clk)) then
		if(count = full_counter) then count <= "0000000000000000";
		else count<=count+'1';
		end if;
        end if;
end process;

process(count(15 downto 14))
    begin
        case count(15 downto 14) is
            when "00" => anod <= not("1110");
            when "01" => anod <= not("1101");
            when "10" => anod <= not("1011");
            when others => anod <= not("0111");
            end case;
end process;

process(count(15 downto 14),digit0,digit1,digit2,digit3)
    begin
        case count(15 downto 14) is
            when "00" => d <= digit0;
            when "01" => d <= digit1;
            when "10" => d <= digit2;
            when others => d <= digit3;
            end case;
end process;

end architecture;

// VHDL entity divizor_frecventa, as the project stores it:
LIBRARY IEEE;
USE IEEE.STD_LOGIC_1164.ALL;


entity divizor_frecventa is
port (clk_in : in std_logic;
       clk_out : out std_logic
     );
end divizor_frecventa;

architecture Behavioral of divizor_frecventa is

signal count : integer :=0;
signal b : std_logic :='0';
begin

 --clk generation.For 100 MHz clock this generates 1 Hz clock.
process(clk_in) 
begin
if(rising_edge(clk_in)) then
count <=count+1;
if(count = 50000000-1) then
b <= not b;
count <=0;

end if;
end if;
clk_out<=b;
end process;
end;

// VHDL entity register_16bit, as the project stores it:
Library IEEE;
use IEEE.std_logic_1164.all;
use ieee.std_logic_unsigned.all;

entity register_16bit is 
	port(
		input: in std_logic_vector(15 downto 0);
		clk: in std_logic;
		output: out std_logic_vector(15 downto 0)
	);
end register_16bit;

architecture arh of register_16bit is 

begin

	process(clk)
	
	begin
		if clk='1' and clk'event then 
			output<=input;		
		end if;
	end process;

end arh;

// VHDL entity dmux, as the project stores it:
--------------------------------------------------------------------------------
-- Project :
-- File    :
-- Autor   :
-- Date    :
--
--------------------------------------------------------------------------------
-- Description :
--
--------------------------------------------------------------------------------

LIBRARY ieee;
USE ieee.std_logic_1164.all;

ENTITY dmux IS
  PORT (
  input: in std_logic_vector(15 downto 0);
  adunare, inmultire, impartire ,egal: in std_logic;
  output1, output2: out std_logic_vector(15 downto 0);
  operatie_aleasa: out std_logic_vector(2 downto 0)
    );
END dmux;

--------------------------------------------------------------------------------
--Complete your VHDL description below
--------------------------------------------------------------------------------

ARCHITECTURE TypeArchitecture OF dmux IS

BEGIN
	process(adunare, inmultire, impartire ,egal)
	variable aux: std_logic_vector(2 downto 0);
	begin
		if adunare='1' then output1<=input;
		aux:="001";
		end if;

		if inmultire='1' then output1<=input;
		aux:="010";
		end if;

		if impartire='1' then output1<=input;
		aux:="100";
		end if;

		if egal='1' then 
			output2<=input;
			operatie_aleasa<=aux;
		end if;
	end process;
END TypeArchitecture;

// VHDL entity bcd_bin, as the project stores it:
library IEEE;
use IEEE.STD_LOGIC_1164.ALL;
use IEEE.STD_LOGIC_ARITH.ALL;
use IEEE.STD_LOGIC_UNSIGNED.ALL;



entity bcd_bin is
    Port ( bcd_in_0 : in  STD_LOGIC_VECTOR (3 downto 0);
           bcd_in_10 : in  STD_LOGIC_VECTOR (3 downto 0);
           bcd_in_100 : in  STD_LOGIC_VECTOR (3 downto 0);
           bcd_in_1000 : in  STD_LOGIC_VECTOR (3 downto 0);
           semn: in std_logic;
           bin_out : out  STD_LOGIC_VECTOR (15 downto 0));
end bcd_bin;

architecture Behavioral of bcd_bin is

begin

process

variable aux: std_logic_vector(15 downto 0);

begin
	aux := (bcd_in_0 * "01")  --multiply by 1
                + (bcd_in_10 * "1010") --multiply by 10
                + (bcd_in_100 * "1100100") --multiply by 100
                + (bcd_in_1000 * "001111101000"); --multiply by 1000
	aux(15):=semn;
	
	bin_out<=aux;

end process;

end Behavioral;

// VHDL entity mux, as the project stores it:
LIBRARY ieee;
USE ieee.std_logic_1164.all;
use ieee.std_logic_unsigned.all;

ENTITY mux IS
  PORT (
  	input1, input2: in std_logic_vector(15 downto 0);
  	sel: in std_logic;
  	mode: out std_logic;
  	output: out std_logic_vector(15 downto 0)
    );
END mux;

--------------------------------------------------------------------------------
--Complete your VHDL description below
--------------------------------------------------------------------------------

ARCHITECTURE TypeArchitecture OF mux IS
BEGIN
	process
	variable aux:std_logic:='1';
	begin
		if sel='1' then aux:=not(aux);
		else aux:=aux;
		end if;

		if aux='0' then output<=input1;
		elsif aux='1' then output<=input2;
		end if;

		mode<=aux;
	end process;

END TypeArchitecture;

// VHDL entity bin_bcd, as the project stores it:
library ieee;
use ieee.std_logic_1164.all;
use ieee.numeric_std.all;

entity bin_bcd is
    port ( 
        input:      in   std_logic_vector (15 downto 0);
        ones:       out  std_logic_vector (3 downto 0);
        tens:       out  std_logic_vector (3 downto 0);
        hundreds:   out  std_logic_vector (3 downto 0);
        thousands:  out  std_logic_vector (3 downto 0);
        semn: out std_logic
    );
end bin_bcd;

architecture arh of bin_bcd is
	signal aux: std_logic_vector(15 downto 0):='0'&input(14 downto 0);
    alias Hex_Display_Data: std_logic_vector (15 downto 0) is aux;
    alias rpm_1:    std_logic_vector (3 downto 0) is ones;
    alias rpm_10:   std_logic_vector (3 downto 0) is tens;
    alias rpm_100:  std_logic_vector (3 downto 0) is hundreds;
    alias rpm_1000: std_logic_vector (3 downto 0) is thousands;
begin
    process (input)
        type fourbits is array (3 downto 0) of std_logic_vector(3 downto 0);
        variable bcd:   std_logic_vector (15 downto 0);
        variable bint:  std_logic_vector (13 downto 0);
    begin
        bcd := (others => '0');     
        bint := Hex_Display_Data (13 downto 0); 

        for i in 0 to 13 loop
            bcd(15 downto 1) := bcd(14 downto 0);
            bcd(0) := bint(13);
            bint(13 downto 1) := bint(12 downto 0);
            bint(0) := '0';

            if i < 13 and bcd(3 downto 0) > "0100" then
                bcd(3 downto 0) := 
                    std_logic_vector (unsigned(bcd(3 downto 0)) + 3);
            end if;
            if i < 13 and bcd(7 downto 4) > "0100" then
                bcd(7 downto 4) := 
                    std_logic_vector(unsigned(bcd(7 downto 4)) + 3);
            end if;
            if i < 13 and bcd(11 downto 8) > "0100" then
                bcd(11 downto 8) := 
                    std_logic_vector(unsigned(bcd(11 downto 8)) + 3);
            end if;
            if i < 13 and bcd(15 downto 12) > "0100" then
                bcd(11 downto 8) := 
                    std_logic_vector(unsigned(bcd(15 downto 12)) + 3);
            end if;
        end loop;

        (rpm_1000, rpm_100, rpm_10, rpm_1)  <= 
                  fourbits'( bcd (15 downto 12), bcd (11 downto 8), 
                               bcd ( 7 downto  4), bcd ( 3 downto 0) );
        semn<=input(15);
    end process ;
end architecture;

// VHDL entity debouncer, as the project stores it:
library IEEE;
    use IEEE.std_logic_1164.all;
    use IEEE.numeric_std.all;

entity debouncer is
    port(    clk : in std_logic;
             btn : in std_logic;
         btn_clr : out std_logic);
end debouncer;

architecture behavioural of debouncer is

    constant delay : integer := 650000; -- 6.5ms
    signal count : integer := 0;
    signal btn_tmp : std_logic := '0';

    begin

    process(clk)
    begin
        if rising_edge(clk) then
            if (btn /= btn_tmp) then
                btn_tmp <= btn;
                count <= 0;
            elsif (count = delay) then
                btn_clr <= btn_tmp;
            else
                count <= count + 1;
            end if;
        end if;
    end process;

end behavioural;

// VHDL entity sumator_scazator, as the project stores it:
library IEEE;
use IEEE.STD_LOGIC_1164.ALL;
use ieee.std_logic_unsigned.all;

entity sumator_scazator is
    port(a, b: in std_logic_vector(15 downto 0);
        res: out std_logic_vector(15 downto 0)
        );
end sumator_scazator;

architecture Behavioral of sumator_scazator is
begin
    process(b)
    variable aux:std_logic_vector(15 downto 0);
    begin
    aux:=x"0000";
   
            if a(15) = '1' and b(15) = '0' then
                if a(14 downto 0) > b(14 downto 0) then
                    aux(14 downto 0):=a(14 downto 0)-b(14 downto 0);
                    aux(15):= '1';
                else 
                    aux(14 downto 0):=b(14 downto 0) - a(14 downto 0);
                    aux(15):='0';
                end if;
            elsif a(15) = '0' and b(15) = '1' then
                if b(14 downto 0) > a(14 downto 0) then
                    aux(14 downto 0):=b(14 downto 0)-a(14 downto 0);
                    aux(15):= '1';
                else 
                    aux(14 downto 0):=a(14 downto 0) - b(14 downto 0);
                    aux(15):='0';
                end if;          
            elsif a(15)='1' and b(15)='1' then
                    aux(14 downto 0):=a(14 downto 0)+b(14 downto 0);
                    aux(15) := '1';
            else 
                    aux(14 downto 0):=a(14 downto 0) + b(14 downto 0);
                    aux(15):='0';
            end if;
        res<=aux;
    end process;
end Behavioral;

// VHDL entity booth_multiplier, as the project stores it:
LIBRARY ieee;
USE ieee.std_logic_1164.ALL;
USE ieee.std_logic_signed.ALL;

ENTITY booth_multiplier IS

	
	
	PORT(m : IN STD_LOGIC_VECTOR(15 DOWNTO 0);
	     r : IN STD_LOGIC_VECTOR(15 DOWNTO 0);
	     result : OUT STD_LOGIC_VECTOR(15 DOWNTO 0));
		  
END booth_multiplier;

ARCHITECTURE behavior OF booth_multiplier IS

BEGIN
	
	PROCESS(r)
		
		CONSTANT X_ZEROS : STD_LOGIC_VECTOR(15 DOWNTO 0) := (OTHERS => '0');
		CONSTANT Y_ZEROS : STD_LOGIC_VECTOR(15 DOWNTO 0) := (OTHERS => '0');
		
		VARIABLE a, s, p : STD_LOGIC_VECTOR(33 DOWNTO 0);
		VARIABLE mn      : STD_LOGIC_VECTOR(15 DOWNTO 0);
	
	BEGIN
		
		a := (OTHERS => '0');
		s := (OTHERS => '0');
		p := (OTHERS => '0');
		
		IF (m /= X_ZEROS AND r /= Y_ZEROS) THEN
			
			a(32 DOWNTO 17) := m;
			a(33) := m(15);
			
			mn := (NOT m) + 1;
			
			s(32 DOWNTO 17) := mn;
			s(33) := NOT(m(15));
			
			p(16 DOWNTO 1) := r;
			
			FOR i IN 1 TO 16 LOOP
				
				IF (p(1 DOWNTO 0) = "01") THEN
					p := p + a;
				ELSIF (p(1 DOWNTO 0) = "10") THEN
					p := p + s;
				END IF;
				
				-- Shift Right Arithmetic
				p(32 DOWNTO 0) := p(33 DOWNTO 1);
			
			END LOOP;
			
		END IF;
		
		result(14 downto 0) <= p(15 DOWNTO 1);
		result(15) <= P(33);
		
	END PROCESS;
	
END behavior;

// VHDL entity impartire, as the project stores it:
library IEEE;
USE IEEE.STD_LOGIC_1164.ALL;
USE IEEE.NUMERIC_STD.ALL;

entity impartire is
port(
    X   : in STD_LOGIC_VECTOR(15 downto 0);
    Y   : in STD_LOGIC_VECTOR(15 downto 0);
    R   : out STD_LOGIC_VECTOR(15 downto 0)
);
end impartire;

architecture Behavioral of impartire is
begin

process(Y)
begin
	R(14 downto 0) <= std_logic_vector(to_signed(to_integer(signed(X(14 downto 0)) / signed(Y(14 downto 0))),15));
	R(15)<= x(15) xor y(15);
end process;
end Behavioral;

// VHDL entity mux_ue, as the project stores it:
--------------------------------------------------------------------------------
-- Project :
-- File    :
-- Autor   :
-- Date    :
--
--------------------------------------------------------------------------------
-- Description :
--
--------------------------------------------------------------------------------

LIBRARY ieee;
USE ieee.std_logic_1164.all;

ENTITY mux_ue IS
  PORT (
  input1, input2, input3: in std_logic_vector(15 downto 0);
  salvare: in std_logic;
  sel: in std_logic_vector(2 downto 0);
  output: out std_logic_vector(15 downto 0)
    );
END mux_ue;

--------------------------------------------------------------------------------
--Complete your VHDL description below
--------------------------------------------------------------------------------

ARCHITECTURE TypeArchitecture OF mux_ue IS

BEGIN
	process(salvare)
	begin
		if salvare='1' then 
		case sel is 
			when "001" => output<=input1;
			when "010" => output<=input2;
			when others=>output<=input3;
		end case;
		end if;
	end process;

END TypeArchitecture;

// VHDL entity register_3bit, as the project stores it:
Library IEEE;
use IEEE.std_logic_1164.all;
use ieee.std_logic_unsigned.all;

entity register_3bit is 
	port(
		input: in std_logic_vector(2 downto 0);
		clk: in std_logic;
		output: out std_logic_vector(2 downto 0)
	);
end register_3bit;

architecture arh of register_3bit is 

begin

	process(clk)
	
	begin
		if clk='1' and clk'event then 
			output<=input;		
		end if;
	end process;

end arh;
